# Fritzing sketch SdCard (saved by Fritzing 0.9.3b)

parts:
  Part1 = Arduino Zero
  microSD_Transflash1 = SparkFun - microSD Transflash

nets:
  N1: Part1.ICSP_MISO, microSD_Transflash1.DO
  N2: Part1.ICSP_SCK, microSD_Transflash1.SCK
  N3: Part1.ICSP_MOSI, microSD_Transflash1.DI
  3V3: Part1.3V3, microSD_Transflash1.VCC
  GND: Part1.GND, microSD_Transflash1.GND

custom parts:
  Arduino Zero: Arduino Zero is a simple and powerful 32-bit extension of the platform established by Arduino UNO. The Zero board aims to provide creative individuals with the potential to realize truly innovative ideas for smart IoT devices, wearable technology, high-tech automation, crazy robotics, and projects not yet imagined. The board is powered by Atmel’s SAMD21 MCU, which features a 32-bit ARM Cortex®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
