# Fritzing sketch IP_Drive (saved by Fritzing 0.9.3b)
breadboards: 1
perfboards: 1

parts:
  Part1 = Arduino Zero
  MTCH112 = IC, DIP package, 8 pins [chip_label=IC]  # not connected
  HV852 = IC, DIP package, 8 pins [chip_label=IC]  # not connected
  C1 = Electrolytic Capacitor [capacitance=1µF package="100 mil [THT, electrolytic]"]  # not connected
  R1 = Resistor [tolerance=±5% resistance=220 package=THT]
  C2 = Electrolytic Capacitor [capacitance=1µF package="100 mil [THT, electrolytic]"]  # not connected
  U1 = CAPSENSE_PAD [package=capsense_pad]
  U2 = CAPSENSE_PAD [package=capsense_pad]
  Part2 = Adafruit MAX98357A I2S 3W Class D Amplifier [part_number="Adafruit #3006"]
  SP1 = SPEAKER [package=pcb_mount_speaker]  # not connected
  U3 = AD8561 - Ultrafast 7ns Single Supply Comparator [part_number=AD8561]
  Thermochromic = Resistor [tolerance=±5% resistance=220 package=THT]
  HV853 = IC, DIP package, 8 pins [chip_label=IC]  # not connected
  HV854 = IC, DIP package, 8 pins [chip_label=IC]  # not connected
  HV855 = IC, DIP package, 8 pins [chip_label=IC]  # not connected
  HV856 = IC, DIP package, 8 pins [chip_label=IC]  # not connected
  HV857 = IC, DIP package, 8 pins [chip_label=IC]  # not connected
  C3 = Electrolytic Capacitor [capacitance=1µF package="100 mil [THT, electrolytic]"]  # not connected
  C4 = Electrolytic Capacitor [capacitance=1µF package="100 mil [THT, electrolytic]"]  # not connected
  C5 = Electrolytic Capacitor [capacitance=1µF package="100 mil [THT, electrolytic]"]  # not connected
  C6 = Electrolytic Capacitor [capacitance=1µF package="100 mil [THT, electrolytic]"]  # not connected

nets:
  5V: Part1.5V, R1.Pin_0, Part2.VIN, U3.V+, Thermochromic.Pin_1
  N1: Part1.D9_PWM, Part2.DIN
  N2: Part1.D0/RX, Part2.LRCLK
  N3: Part1.D1/TX, Part2.BCLK
  N4: Part1.D6_PWM, U3.+IN
  GND: Part1.GND, U1.RECEIVE, U2.RECEIVE, Part2.GND, U3.-IN, U3.GND
  N5: U3.OUT, Thermochromic.Pin_0

custom parts:
  Arduino Zero: Arduino Zero is a simple and powerful 32-bit extension of the platform established by Arduino UNO. The Zero board aims to provide creative individuals with the potential to realize truly innovative ideas for smart IoT devices, wearable technology, high-tech automation, crazy robotics, and projects not yet imagined. The board is powered by Atmel’s SAMD21 MCU, which features a 32-bit ARM Cortex®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
  Adafruit MAX98357A I2S 3W Class D Amplifier: Listen to this good news - we now have an all in one digital audio amp breakout board that works incredibly well with the Raspberry Pi! If you're looking for an easy and low cost way to get you digital sound files bumpin' then the MAX08357 I2S Amp Breakout is for you. It takes standard I2S digital audio input and, not only decodes it into analog, but also amplifies it directly into a speaker.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
